# Fritzing sketch circuitDiagram (saved by Fritzing 0.9.4)
breadboards: 1

parts:
  Part1 = Arduino Uno (Rev3)
  J1 = Basic Servo
  J2 = Basic Servo
  J3 = Basic Servo
  WeMos_D1_Mini_Relay_Shield1 = WeMos D1 Mini Relay Shield
  WeMos_D1_Mini_Relay_Shield2 = WeMos D1 Mini Relay Shield
  M1 = DC Motor
  U1 = LIPO-1000mAh [package=lipo-1000]
  U2 = LIPO-1000mAh [package=lipo-1000]
  U3 = LIPO-1000mAh [package=lipo-1000]
  HC-SR04_Sensor_1 = HC-SR04 Ultrasonic Distance Sensor
  HC-SR04_Sensor_2 = HC-SR04 Ultrasonic Distance Sensor
  U4 = TRANSCHIPTC5747 [package=camera_sfv24r-2st_2]
  M3 = DC Motor
  M4 = DC Motor

nets:
  N1: Part1.D8, WeMos_D1_Mini_Relay_Shield1.RST
  N2: Part1.D9_PWM, WeMos_D1_Mini_Relay_Shield2.RST
  N3: Part1.D10_PWM/SS, U4.SHIELD
  N4: Part1.D11_PWM/MOSI, U4.LED_CTRL
  N5: Part1.D12/MISO, J2.pulse
  N6: Part1.D3_PWM, J1.pulse, J3.pulse
  N7: Part1.D4, HC-SR04_Sensor_1.TRIG
  N8: Part1.D5_PWM, HC-SR04_Sensor_1.ECHO
  N9: Part1.D6_PWM, HC-SR04_Sensor_2.TRIG
  N10: Part1.D7, HC-SR04_Sensor_2.ECHO
  VCC: Part1.5V, J1.vcc, J2.vcc, J3.vcc, WeMos_D1_Mini_Relay_Shield1.5V, WeMos_D1_Mini_Relay_Shield2.5V, HC-SR04_Sensor_1.VCC, HC-SR04_Sensor_2.VCC, U4.SCLK
  GND: Part1.GND, J1.gnd, J2.gnd, J3.gnd, WeMos_D1_Mini_Relay_Shield1.G, WeMos_D1_Mini_Relay_Shield2.G, U4.AGND
  N11: WeMos_D1_Mini_Relay_Shield1.COM, M3.pin_1
  N12: WeMos_D1_Mini_Relay_Shield1.NO, U3.+
  N13: WeMos_D1_Mini_Relay_Shield2.COM, M1.pin_1, M4.pin_1
  N14: WeMos_D1_Mini_Relay_Shield2.NO, U1.+
  N15: M1.pin_2, U2.-, M4.pin_2
  N16: U1.-, U2.+
  N17: U3.-, M3.pin_2
  GND_2: HC-SR04_Sensor_1.GND, HC-SR04_Sensor_2.GND

notes:
  船体运动舵机（方向控制）
  HC-SR04（左右距离检测）
  直流电机（传递垃圾）
  DFRobot 人工智能摄像头
  直流电机（动力驱动）
  伺服电机（清理垃圾）
